// Logisim project assign1.circ as structural Verilog: 10 circuits, main circuit main
module main (
  input  W,
  input  X,
  input  Y,
  input  Z
);

  wire a_1_out_5, b_1_out_5, c_1_out_5, d_1_out_5, e_1_out_5, f_1_out_5, g_1_out_5, h_1_out_5, i_1_out_5;

  C c_1 (.W(W), .X(X), .Y(Y), .Z(Z), .out_5(c_1_out_5));
  B b_1 (.W(W), .X(X), .Y(Y), .Z(Z), .out_5(b_1_out_5));
  A a_1 (.W(W), .X(X), .Y(Y), .Z(Z), .out_5(a_1_out_5));
  D d_1 (.W(W), .X(X), .Y(Y), .Z(Z), .out_5(d_1_out_5));
  E e_1 (.W(W), .X(X), .Y(Y), .Z(Z), .out_5(e_1_out_5));
  F f_1 (.W(W), .X(X), .Y(Y), .Z(Z), .out_5(f_1_out_5));
  G g_1 (.W(W), .X(X), .Y(Y), .Z(Z), .out_5(g_1_out_5));
  H h_1 (.W(W), .X(X), .Y(Y), .Z(Z), .out_5(h_1_out_5));
  I i_1 (.W(W), .X(X), .Y(Y), .Z(Z), .out_5(i_1_out_5));
  LED led_1 (.in(a_1_out_5));
  LED led_2 (.in(d_1_out_5));
  LED led_3 (.in(g_1_out_5));
  LED led_4 (.in(b_1_out_5));
  LED led_5 (.in(e_1_out_5));
  LED led_6 (.in(h_1_out_5));
  LED led_7 (.in(c_1_out_5));
  LED led_8 (.in(f_1_out_5));
  LED led_9 (.in(i_1_out_5));

  // Notes on the sheet:
  //   A
  //   D
  //   G
  //   B
  //   E
  //   H
  //   C
  //   F
  //   I
endmodule

module A (
  input  W,
  input  X,
  input  Y,
  input  Z,
  output out_5
);

  wire and_1_out, and_2_out, and_3_out, and_4_out, and_5_out, not_1_out, not_2_out, not_3_out, not_4_out;

  not not_1 (not_1_out, W);
  not not_2 (not_2_out, X);
  not not_3 (not_3_out, Y);
  not not_4 (not_4_out, Z);
  and and_1 (and_1_out, W, not_3_out);
  and and_2 (and_2_out, not_2_out, Y, Z);
  and and_3 (and_3_out, not_1_out, Y, Z);
  and and_4 (and_4_out, not_4_out, W, X);
  and and_5 (and_5_out, not_2_out, not_3_out, not_4_out);
  or or_1 (out_5, and_1_out, and_2_out, and_3_out, and_4_out, and_5_out);

  // Notes on the sheet:
  //   A=WY'+X'YZ+W'YZ+WXZ'+X'Y'Z'
endmodule

module B (
  input  W,
  input  X,
  input  Y,
  input  Z,
  output out_5
);

  wire and_1_out, and_2_out, and_3_out, and_4_out, not_1_out, not_2_out, not_3_out, not_4_out;

  not not_1 (not_1_out, W);
  not not_2 (not_2_out, X);
  not not_3 (not_3_out, Y);
  not not_4 (not_4_out, Z);
  and and_1 (and_1_out, not_2_out, not_3_out, not_4_out);
  and and_2 (and_2_out, W, Y, not_4_out);
  and and_3 (and_3_out, not_1_out, not_3_out, not_4_out);
  and and_4 (and_4_out, W, not_2_out, Y);
  or or_1 (out_5, and_1_out, and_2_out, and_3_out, and_4_out);

  // Notes on the sheet:
  //   B=X'Y'Z'+WYZ'+W'Y'Z'+WX'Y
endmodule

module C (
  input  W,
  input  X,
  input  Y,
  input  Z,
  output out_5
);

  wire and_1_out, and_2_out, and_3_out, and_4_out, and_5_out, not_1_out, not_2_out, not_3_out;

  not not_1 (not_1_out, X);
  not not_2 (not_2_out, Y);
  not not_3 (not_3_out, Z);
  and and_1 (and_1_out, W, not_2_out);
  and and_2 (and_2_out, X, Y, not_3_out);
  and and_3 (and_3_out, not_1_out, not_2_out, not_3_out);
  and and_4 (and_4_out, X, not_2_out, Z);
  and and_5 (and_5_out, W, not_1_out, Z);
  or or_1 (out_5, and_1_out, and_2_out, and_3_out, and_4_out, and_5_out);

  // Notes on the sheet:
  //   C=WY'+XYZ'+X'Y'Z'+XY'Z+WX'Z
endmodule

module D (
  input  W,
  input  X,
  input  Y,
  input  Z,
  output out_5
);

  wire and_1_out, and_2_out, and_3_out, and_4_out, not_1_out, not_2_out, not_3_out, not_4_out;

  not not_1 (not_1_out, W);
  not not_2 (not_2_out, X);
  not not_3 (not_3_out, Y);
  not not_4 (not_4_out, Z);
  and and_1 (and_1_out, not_1_out, not_2_out, Z);
  and and_2 (and_2_out, W, X, not_4_out);
  and and_3 (and_3_out, not_2_out, not_3_out, Z);
  and and_4 (and_4_out, W, Y, not_4_out);
  or or_1 (out_5, and_1_out, and_2_out, and_3_out, and_4_out);

  // Notes on the sheet:
  //   D=W'X'Z+WXZ'+X'Y'Z+WYZ'
endmodule

module E (
  input  W,
  input  X,
  input  Y,
  input  Z,
  output out_5
);

  wire and_1_out, and_2_out, and_3_out, and_4_out, and_5_out, not_1_out, not_2_out, not_3_out, not_4_out;

  not not_1 (not_1_out, W);
  not not_2 (not_2_out, X);
  not not_3 (not_3_out, Y);
  not not_4 (not_4_out, Z);
  and and_1 (and_1_out, not_1_out, X, not_4_out);
  and and_2 (and_2_out, X, Y, Z);
  and and_3 (and_3_out, W, X, not_3_out);
  and and_4 (and_4_out, W, not_2_out, Y);
  and and_5 (and_5_out, not_1_out, not_2_out, not_3_out, Z);
  or or_1 (out_5, and_1_out, and_2_out, and_3_out, and_4_out, and_5_out);

  // Notes on the sheet:
  //   E=W'XZ'+XYZ+WXY'+WX'Y+W'X'Y'Z
endmodule

module F (
  input  W,
  input  X,
  input  Y,
  input  Z,
  output out_5
);

  wire and_1_out, and_2_out, and_3_out, and_4_out, not_1_out, not_2_out, not_3_out, not_4_out;

  not not_1 (not_1_out, W);
  not not_2 (not_2_out, X);
  not not_3 (not_3_out, Y);
  not not_4 (not_4_out, Z);
  and and_1 (and_1_out, not_2_out, not_3_out, Z);
  and and_2 (and_2_out, W, X, not_4_out);
  and and_3 (and_3_out, not_1_out, not_3_out, Z);
  and and_4 (and_4_out, W, Y, not_4_out);
  or or_1 (out_5, and_1_out, and_2_out, and_3_out, and_4_out);

  // Notes on the sheet:
  //   F=X'Y'Z+WXZ'+W'Y'Z+WYZ'
endmodule

module G (
  input  W,
  input  X,
  input  Y,
  input  Z,
  output out_5
);

  wire and_1_out, and_2_out, and_3_out, and_4_out, not_1_out, not_2_out, not_3_out, not_4_out;

  not not_1 (not_1_out, W);
  not not_2 (not_2_out, X);
  not not_3 (not_3_out, Y);
  not not_4 (not_4_out, Z);
  and and_1 (and_1_out, W, not_3_out);
  and and_2 (and_2_out, not_1_out, not_2_out, Y);
  and and_3 (and_3_out, X, Y, not_4_out);
  and and_4 (and_4_out, not_2_out, Y, Z);
  or or_1 (out_5, and_1_out, and_2_out, and_3_out, and_4_out);

  // Notes on the sheet:
  //   G=WY'+W'X'Y+XYZ'+X'YZ
endmodule

module H (
  input  W,
  input  X,
  input  Y,
  input  Z,
  output out_5
);

  wire and_1_out, and_2_out, and_3_out, and_4_out, and_5_out, not_1_out, not_2_out, not_3_out, not_4_out;

  not not_1 (not_1_out, W);
  not not_2 (not_2_out, X);
  not not_3 (not_3_out, Y);
  not not_4 (not_4_out, Z);
  and and_1 (and_1_out, not_2_out, Y, not_4_out);
  and and_2 (and_2_out, W, Y, not_4_out);
  and and_3 (and_3_out, W, not_2_out, not_4_out);
  and and_4 (and_4_out, W, not_2_out, Y);
  and and_5 (and_5_out, not_1_out, X, not_3_out, not_4_out);
  or or_1 (out_5, and_1_out, and_2_out, and_3_out, and_4_out, and_5_out);

  // Notes on the sheet:
  //   H=X'YZ'+WYZ'+WX'Z'+WX'Y+W'XY'Z'
endmodule

module I (
  input  W,
  input  X,
  input  Y,
  input  Z,
  output out_5
);

  wire and_1_out, and_2_out, and_3_out, and_4_out, and_5_out, not_1_out, not_2_out, not_3_out, not_4_out;

  not not_1 (not_1_out, W);
  not not_2 (not_2_out, X);
  not not_3 (not_3_out, Y);
  not not_4 (not_4_out, Z);
  and and_1 (and_1_out, W, not_3_out);
  and and_2 (and_2_out, not_1_out, X, Z);
  and and_3 (and_3_out, W, X, not_4_out);
  and and_4 (and_4_out, W, not_2_out, Z);
  and and_5 (and_5_out, not_1_out, not_2_out, Y, not_4_out);
  or or_1 (out_5, and_1_out, and_2_out, and_3_out, and_4_out, and_5_out);

  // Notes on the sheet:
  //   I=WY'+W'XZ+WXZ'+WX'Z+W'X'YZ'
endmodule
