// Logisim project assign2.circ as structural Verilog: 1 circuit, main circuit main
module main (
  input  x__Direction
);

  wire and_1_out, and_2_out, and_3_out, and_4_out, and_5_out, and_6_out, and_7_out, and_8_out, and_9_out,
       and_10_out, and_11_out, and_12_out, and_13_out, and_14_out, and_15_out, and_16_out, and_17_out,
       and_18_out, and_19_out, and_20_out, and_21_out, and_22_out, and_23_out, and_24_out, and_25_out,
       and_26_out, and_27_out, and_28_out, and_29_out, and_30_out, and_31_out, and_32_out, clock_1_out,
       j_k_ff_1_q, j_k_ff_2_q, j_k_ff_3_q, j_k_ff_4_q, not_1_out, not_2_out, not_3_out, not_4_out, not_5_out,
       not_6_out, not_7_out, not_8_out, not_9_out, not_10_out, not_11_out, not_12_out, not_13_out,
       not_14_out, not_15_out, not_16_out, not_17_out, not_18_out, not_19_out, not_20_out, not_21_out,
       not_22_out, not_23_out, not_24_out, not_25_out, not_26_out, not_27_out, not_28_out, not_29_out,
       not_30_out, not_31_out, not_32_out, not_33_out, not_34_out, not_35_out, not_36_out, not_37_out,
       not_38_out, not_39_out, not_40_out, not_41_out, not_42_out, not_43_out, not_44_out, not_45_out,
       not_46_out, not_47_out, not_48_out, not_49_out, not_50_out, not_51_out, not_52_out, not_53_out,
       not_54_out, not_55_out, not_56_out, not_57_out, not_58_out, not_59_out, not_60_out, not_61_out,
       not_62_out, not_63_out, not_64_out, or_1_out, or_2_out, or_3_out, or_4_out, or_5_out, or_6_out,
       or_7_out, or_8_out;

  Clock clock_1 (.out(clock_1_out));
  not not_1 (not_1_out, x__Direction);
  not not_2 (not_2_out, x__Direction);
  not not_3 (not_3_out, x__Direction);
  not not_4 (not_4_out, x__Direction);
  not not_5 (not_5_out, x__Direction);
  not not_6 (not_6_out, x__Direction);
  not not_7 (not_7_out, x__Direction);
  not not_8 (not_8_out, x__Direction);
  not not_9 (not_9_out, x__Direction);
  not not_10 (not_10_out, x__Direction);
  not not_11 (not_11_out, x__Direction);
  not not_12 (not_12_out, x__Direction);
  not not_13 (not_13_out, x__Direction);
  not not_14 (not_14_out, x__Direction);
  not not_15 (not_15_out, x__Direction);
  not not_16 (not_16_out, x__Direction);
  not not_17 (not_17_out, j_k_ff_4_q);
  not not_18 (not_18_out, j_k_ff_4_q);
  not not_19 (not_19_out, j_k_ff_4_q);
  not not_20 (not_20_out, j_k_ff_4_q);
  not not_21 (not_21_out, j_k_ff_4_q);
  not not_22 (not_22_out, j_k_ff_4_q);
  not not_23 (not_23_out, j_k_ff_4_q);
  not not_24 (not_24_out, j_k_ff_4_q);
  not not_25 (not_25_out, j_k_ff_3_q);
  not not_26 (not_26_out, j_k_ff_3_q);
  not not_27 (not_27_out, j_k_ff_3_q);
  not not_28 (not_28_out, j_k_ff_3_q);
  not not_29 (not_29_out, j_k_ff_3_q);
  not not_30 (not_30_out, j_k_ff_3_q);
  not not_31 (not_31_out, j_k_ff_3_q);
  not not_32 (not_32_out, j_k_ff_3_q);
  not not_33 (not_33_out, j_k_ff_3_q);
  not not_34 (not_34_out, j_k_ff_3_q);
  not not_35 (not_35_out, j_k_ff_3_q);
  not not_36 (not_36_out, j_k_ff_3_q);
  not not_37 (not_37_out, j_k_ff_2_q);
  not not_38 (not_38_out, j_k_ff_2_q);
  not not_39 (not_39_out, j_k_ff_2_q);
  not not_40 (not_40_out, j_k_ff_2_q);
  not not_41 (not_41_out, j_k_ff_2_q);
  not not_42 (not_42_out, j_k_ff_2_q);
  not not_43 (not_43_out, j_k_ff_2_q);
  not not_44 (not_44_out, j_k_ff_2_q);
  not not_45 (not_45_out, j_k_ff_2_q);
  not not_46 (not_46_out, j_k_ff_2_q);
  not not_47 (not_47_out, j_k_ff_2_q);
  not not_48 (not_48_out, j_k_ff_2_q);
  not not_49 (not_49_out, j_k_ff_2_q);
  not not_50 (not_50_out, j_k_ff_2_q);
  not not_51 (not_51_out, j_k_ff_1_q);
  not not_52 (not_52_out, j_k_ff_1_q);
  not not_53 (not_53_out, j_k_ff_1_q);
  not not_54 (not_54_out, j_k_ff_1_q);
  not not_55 (not_55_out, j_k_ff_1_q);
  not not_56 (not_56_out, j_k_ff_1_q);
  not not_57 (not_57_out, j_k_ff_1_q);
  not not_58 (not_58_out, j_k_ff_1_q);
  not not_59 (not_59_out, j_k_ff_1_q);
  not not_60 (not_60_out, j_k_ff_1_q);
  not not_61 (not_61_out, j_k_ff_1_q);
  not not_62 (not_62_out, j_k_ff_1_q);
  not not_63 (not_63_out, j_k_ff_1_q);
  not not_64 (not_64_out, j_k_ff_1_q);
  and and_1 (and_1_out, not_49_out, not_33_out, not_17_out, x__Direction);
  and and_2 (and_2_out, j_k_ff_2_q, not_34_out, not_18_out, not_1_out);
  and and_3 (and_3_out, not_50_out, not_35_out, not_19_out, not_2_out);
  and and_4 (and_4_out, j_k_ff_2_q, not_36_out, not_20_out, x__Direction);
  and and_5 (and_5_out, not_51_out, j_k_ff_3_q, not_21_out, not_3_out);
  and and_6 (and_6_out, j_k_ff_1_q, j_k_ff_3_q, not_22_out, x__Direction);
  and and_7 (and_7_out, not_52_out, j_k_ff_3_q, not_23_out, x__Direction);
  and and_8 (and_8_out, j_k_ff_1_q, j_k_ff_3_q, not_24_out, not_4_out);
  and and_9 (and_9_out, not_53_out, not_37_out, j_k_ff_4_q, not_5_out);
  and and_10 (and_10_out, not_54_out, j_k_ff_2_q, j_k_ff_4_q, x__Direction);
  and and_11 (and_11_out, j_k_ff_1_q, not_38_out, j_k_ff_4_q, x__Direction);
  and and_12 (and_12_out, j_k_ff_1_q, j_k_ff_2_q, j_k_ff_4_q, not_6_out);
  and and_13 (and_13_out, not_55_out, not_39_out, j_k_ff_4_q, x__Direction);
  and and_14 (and_14_out, not_56_out, j_k_ff_2_q, j_k_ff_4_q, not_7_out);
  and and_15 (and_15_out, j_k_ff_1_q, not_40_out, j_k_ff_4_q, not_8_out);
  and and_16 (and_16_out, j_k_ff_1_q, j_k_ff_2_q, j_k_ff_4_q, x__Direction);
  and and_17 (and_17_out, not_57_out, not_41_out, not_25_out, not_9_out);
  and and_18 (and_18_out, not_58_out, not_42_out, j_k_ff_3_q, x__Direction);
  and and_19 (and_19_out, not_59_out, j_k_ff_2_q, not_26_out, x__Direction);
  and and_20 (and_20_out, not_60_out, j_k_ff_2_q, j_k_ff_3_q, not_10_out);
  and and_21 (and_21_out, j_k_ff_1_q, not_43_out, not_27_out, x__Direction);
  and and_22 (and_22_out, j_k_ff_1_q, not_44_out, j_k_ff_3_q, not_11_out);
  and and_23 (and_23_out, j_k_ff_1_q, j_k_ff_2_q, not_28_out, not_12_out);
  and and_24 (and_24_out, j_k_ff_1_q, j_k_ff_2_q, j_k_ff_3_q, x__Direction);
  and and_25 (and_25_out, not_61_out, not_45_out, not_29_out, x__Direction);
  and and_26 (and_26_out, not_62_out, not_46_out, j_k_ff_3_q, not_13_out);
  and and_27 (and_27_out, not_63_out, j_k_ff_2_q, not_30_out, not_14_out);
  and and_28 (and_28_out, not_64_out, j_k_ff_2_q, j_k_ff_3_q, x__Direction);
  and and_29 (and_29_out, j_k_ff_1_q, not_47_out, not_31_out, not_15_out);
  and and_30 (and_30_out, j_k_ff_1_q, not_48_out, j_k_ff_3_q, x__Direction);
  and and_31 (and_31_out, j_k_ff_1_q, j_k_ff_2_q, not_32_out, x__Direction);
  and and_32 (and_32_out, j_k_ff_1_q, j_k_ff_2_q, j_k_ff_3_q, not_16_out);
  or or_1 (or_1_out, and_1_out, and_2_out);
  or or_2 (or_2_out, and_3_out, and_4_out);
  or or_3 (or_3_out, and_5_out, and_6_out);
  or or_4 (or_4_out, and_7_out, and_8_out);
  or or_5 (or_5_out, and_9_out, and_10_out, and_11_out, and_12_out);
  or or_6 (or_6_out, and_13_out, and_14_out, and_15_out, and_16_out);
  or or_7 (or_7_out, and_17_out, and_18_out, and_19_out, and_20_out, and_21_out, and_22_out, and_23_out, and_24_out);
  or or_8 (or_8_out, and_25_out, and_26_out, and_27_out, and_28_out, and_29_out, and_30_out, and_31_out, and_32_out);
  J_K_Flip_Flop j_k_ff_1 (
    .J(or_1_out), .clk(clock_1_out), .K(or_2_out), .Q(j_k_ff_1_q));  // open: Qn, preset, en, reset
  J_K_Flip_Flop j_k_ff_2 (
    .J(or_3_out), .clk(clock_1_out), .K(or_4_out), .Q(j_k_ff_2_q));  // open: Qn, preset, en, reset
  J_K_Flip_Flop j_k_ff_3 (
    .J(or_5_out), .clk(clock_1_out), .K(or_6_out), .Q(j_k_ff_3_q));  // open: Qn, preset, en, reset
  J_K_Flip_Flop j_k_ff_4 (
    .J(or_7_out), .clk(clock_1_out), .K(or_8_out), .Q(j_k_ff_4_q));  // open: Qn, preset, en, reset
  LED led_1 (.in(j_k_ff_1_q));
  LED led_2 (.in(j_k_ff_2_q));
  LED led_3 (.in(j_k_ff_3_q));
  LED led_4 (.in(j_k_ff_4_q));

  // Notes on the sheet:
  //   J_A
  //   K_A
  //   J_B
  //   K_B
  //   J_C
  //   K_C
  //   J_D
  //   K_D
  //   B'C'D'x
  //   BC'D'x'
  //   B'C'D'x'
  //   BC'D'x
  //   A'CD'x'
  //   ACD'x
  //   A'CD'x
  //   ACD'x'
  //   A'B'Dx'
  //   A'BDx
  //   AB'Dx
  //   ABDx'
  //   A'B'Dx
  //   A'BDx'
  //   AB'Dx'
  //   ABDx
  //   A'B'C'x'
  //   A'B'Cx
  //   A'BC'x
  //   A'BCx'
  //   AB'C'x
  //   AB'Cx'
  //   ABC'x'
  //   ABCx
  //   A'B'C'x
  //   A'B'Cx'
  //   A'BC'x'
  //   A'BCx
  //   AB'C'x'
  //   AB'Cx
  //   ABC'x
  //   ABCx'
  //   A Flip-flop
  //   B Flip-flop
  //   C Flip-flop
  //   D Flip-flop
  //   A
  //   B
  //   C
  //   D
endmodule
